# Fritzing sketch SchemaAssemblaggioBase (saved by Fritzing 0.9.3b)
breadboards: 1

parts:
  VCC1 = Battery
  VCC2 = Battery
  C1 = Ceramic Capacitor [capacitance=100nF package="100 mil [THT, multilayer]"]
  C2 = Ceramic Capacitor [capacitance=100nF package="100 mil [THT, multilayer]"]
  U1 = LM 358 Dual Op-Amp [package="DIP8 [THT]"]

nets:
  N1: VCC1.-, VCC2.+, C1.0, C2.1
  N2: VCC1.+, C2.0, U1.connector7
  N3: VCC2.-, C1.1, U1.connector3
