# Fritzing sketch SchemaAssemblaggioCirc1 (saved by Fritzing 0.9.3b)
breadboards: 1

parts:
  VCC1 = Battery
  VCC2 = Battery
  C2 = Ceramic Capacitor [capacitance=100nF package="100 mil [THT, multilayer]"]
  U1 = LM 358 Dual Op-Amp [package="DIP8 [THT]"]
  VCC3 = Battery
  R2 = Resistor [tolerance=±5% resistance=47 package=THT]
  R3 = Resistor [tolerance=±5% resistance=47 package=THT]
  R4 = Resistor [tolerance=±5% resistance=10k package=THT]
  R5 = Resistor [tolerance=±5% resistance=68k package=THT]
  C3 = Ceramic Capacitor [capacitance=100nF package="100 mil [THT, multilayer]"]

nets:
  N1: VCC1.+, C2.0, U1.connector7
  N2: VCC2.-, U1.connector3, C3.1
  N3: VCC2.+, C2.1, U1.connector2, VCC3.-, R2.Pin_1, R3.Pin_1, C3.0
  N4: U1.connector0, R5.Pin_0
  N5: U1.connector1, R4.Pin_0, R5.Pin_1
  N6: VCC3.+, R2.Pin_0, R3.Pin_0, R4.Pin_1
