# Fritzing sketch SchemaAssemblaggioCirc2 (saved by Fritzing 0.9.3b)
breadboards: 1

parts:
  VCC2 = Battery
  U1 = LM 358 Dual Op-Amp [package="DIP8 [THT]"]
  VCC3 = Battery
  R2 = Resistor [tolerance=±5% resistance=47 package=THT]
  R5 = Resistor [tolerance=±5% resistance=220 package=THT]
  R3 = Resistor [tolerance=±5% resistance=47 package=THT]
  R6 = Resistor [tolerance=±5% resistance=220 package=THT]
  C3 = Ceramic Capacitor [capacitance=100nF package="100 mil [THT, multilayer]"]
  VCC1 = Battery
  C4 = Ceramic Capacitor [capacitance=100nF package="100 mil [THT, multilayer]"]
  C5 = Ceramic Capacitor [capacitance=100nF package="100 mil [THT, multilayer]"]

nets:
  N1: VCC2.-, U1.connector3, C3.1
  N2: U1.connector0, R5.Pin_0
  N3: U1.connector1, R5.Pin_1, R6.Pin_0
  N4: U1.connector2, VCC3.-, R2.Pin_1, R3.Pin_1, C3.0, VCC1.-, C4.0
  N5: U1.connector7, VCC1.+, C4.1
  N6: VCC3.+, R2.Pin_0, R3.Pin_0, C5.1
  N7: R6.Pin_1, C5.0

notes:
  V1
  GND
  VOUT
  GEN FX
  CONTINUA
